# Fritzing sketch CarbonSensor (saved by Fritzing 0.9.3b)
breadboards: 1

parts:
  WeMos_D1_Mini1 = WeMos D1 Mini  # not connected
  Squix1 = OLED 0.96" 128x64 I2C SSD1306
  U1 = WS2812 RGB LED strip

nets:
  VCC: Squix1.VCC, U1.VCC
  GND: Squix1.GND, U1.GND

custom parts:
  WS2812 RGB LED strip: WS2812 strip
